// Logisim project CounterT_TT_3.circ as structural Verilog: 1 circuit, main circuit main
module main (
  input  in_1,
  input  in_2,
  input  in_3,
  input  in_4,
  input  in_5,
  input  in_6,
  input  in_7,
  input  in_8,
  output out_9,
  output q1,
  output q2,
  output q3,
  output out_13,
  output u1,
  output u2,
  output u3,
  output q1_2,
  output q2_2,
  output q3_2,
  output u1_2,
  output u2_2,
  output u3_2,
  output q1_3,
  output q2_3,
  output q3_3,
  output u1_3,
  output u2_3,
  output u3_3,
  output q1_4,
  output q2_4,
  output q3_4,
  output u1_4,
  output u2_4,
  output u3_4,
  output q1_5,
  output q2_5,
  output q3_5,
  output u1_5,
  output u2_5,
  output u3_5,
  output out_41,
  output q3_6,
  output q2_6,
  output q1_6,
  output out_45,
  output out_46,
  output out_47,
  output out_48,
  output q1_7,
  output q2_7,
  output q1_8,
  output q3_7,
  output q4,
  output q5,
  output q6,
  output q7,
  output q8,
  output q9,
  output q2_8,
  output q3_8,
  output y4,
  output y3,
  output y2,
  output y1,
  output q4_2,
  output y4_2,
  output y3_2,
  output y2_2,
  output y1_2
);

  wire and_1_out, and_2_out, and_3_out, and_4_out, and_5_out, and_6_out, and_7_out, and_8_out, and_9_out,
       clock_1_out, clock_2_out, clock_3_out, clock_4_out, clock_5_out, clock_6_out, clock_7_out,
       clock_8_out, clock_9_out, in_out, j_k_ff_1_q, j_k_ff_1_qn, j_k_ff_5_q, j_k_ff_5_qn, j_k_ff_8_q,
       j_k_ff_8_qn, j_k_ff_10_q, j_k_ff_10_qn, j_k_ff_11_q, j_k_ff_11_qn, j_k_ff_14_q, j_k_ff_14_qn,
       j_k_ff_15_q, j_k_ff_15_qn, j_k_ff_16_q, j_k_ff_16_qn, j_k_ff_17_q, j_k_ff_17_qn, not_1_out, not_2_out,
       not_3_out, not_4_out, not_5_out, not_6_out, not_7_out, not_8_out, not_9_out, not_10_out, not_11_out,
       not_12_out, not_13_out, or_1_out, or_2_out, s_r_ff_1_q, t_ff_1_q, t_ff_7_q;
  wire [6:0] rom_1_data;
  wire [7:0] counter_6_q;

  Clock clock_1 (.out(clock_1_out));
  Clock clock_2 (.out(clock_2_out));
  Clock clock_3 (.out(clock_3_out));
  Clock clock_4 (.out(clock_4_out));
  Clock clock_5 (.out(clock_5_out));
  Clock clock_6 (.out(clock_6_out));
  J_K_Flip_Flop j_k_ff_1 (
    .J(1'b1), .clk(clock_1_out), .K(1'b1), .Q(j_k_ff_1_q), .Qn(j_k_ff_1_qn));  // open: preset, en, reset
  not not_1 (not_1_out, clock_1_out);
  J_K_Flip_Flop j_k_ff_2 (.J(1'b1), .clk(clock_2_out), .K(1'b1), .Q(q1_3), .Qn(u1_3));  // open: preset, en, reset
  T_Flip_Flop t_ff_1 (.clk(clock_3_out), .T(clock_3_out), .Q(t_ff_1_q));  // open: Qn, preset, reset, en
  Counter #(.width(3), .max('h7)) counter_1 (
    .load(in_2), .Q({q3_6, q2_6, q1_6}), .carry(out_41), .clk(clock_7_out));  // open: D, count, clr
  Clock clock_7 (.out(clock_7_out));
  Counter #(.width(3), .max('h7)) counter_2 (
    .load(in_5), .Q({q3_7, q1_8, q2_7}), .carry(out_46), .clk(clock_4_out));  // open: D, count, clr
  Counter #(.width(4), .max('hf)) counter_3 (
    .Q({y4, y3, y2, y1}), .clk(clock_5_out), .clr(s_r_ff_1_q));  // open: load, D, count, carry
  Counter #(.width(4), .max('hf)) counter_4 (
    .Q({y4_2, y3_2, y2_2, y1_2}), .clk(clock_6_out), .clr(and_5_out));  // open: load, D, count, carry
  J_K_Flip_Flop j_k_ff_3 (
    .J(j_k_ff_1_q), .clk(not_1_out), .K(j_k_ff_1_qn), .Q(q1), .Qn(u1));  // open: preset, en, reset
  J_K_Flip_Flop j_k_ff_4 (.J(1'b1), .clk(q1_3), .K(1'b1), .Q(q2_3), .Qn(u2_3));  // open: preset, en, reset
  T_Flip_Flop t_ff_2 (.clk(clock_3_out), .T(t_ff_1_q), .Q(q1_4), .Qn(u1_4));  // open: preset, reset, en
  and and_1 (and_1_out, q2_7, q1_8, q3_7, clock_4_out);
  J_K_Flip_Flop j_k_ff_5 (.J(1'b1), .clk(q1), .K(1'b1), .Q(j_k_ff_5_q), .Qn(j_k_ff_5_qn));  // open: preset, en, reset
  not not_2 (not_2_out, q1);
  J_K_Flip_Flop j_k_ff_6 (.J(1'b1), .clk(q2_3), .K(1'b1), .Q(q3_3), .Qn(u3_3));  // open: preset, en, reset
  and and_2 (and_2_out, q1_4, t_ff_1_q);
  Counter #(.width(3), .max('h7)) counter_5 (
    .load(in_6), .Q({q6, q5, q4}), .carry(out_47), .clk(and_1_out));  // open: D, count, clr
  not not_3 (not_3_out, y1);
  not not_4 (not_4_out, y3);
  not not_5 (not_5_out, y1_2);
  not not_6 (not_6_out, y3_2);
  J_K_Flip_Flop j_k_ff_7 (
    .J(j_k_ff_5_q), .clk(not_2_out), .K(j_k_ff_5_qn), .Q(q2), .Qn(u2));  // open: preset, en, reset
  T_Flip_Flop t_ff_3 (.clk(clock_3_out), .T(and_2_out), .Q(q2_4), .Qn(u2_4));  // open: preset, reset, en
  Clock clock_8 (.out(clock_8_out));
  and and_3 (and_3_out, q4, q5, q6, and_1_out);
  and and_4 (and_4_out, not_3_out, y2, not_4_out, y4);
  and and_5 (and_5_out, not_5_out, y2_2, not_6_out, y4_2);
  Clock in (.out(in_out));
  and and_6 (and_6_out, q2_4, and_2_out);
  Counter #(.ongoal("stay")) counter_6 (
    .load(in_3), .Q(counter_6_q), .carry(out_45), .clk(clock_8_out), .clr(in_4));  // open: D, count
  Counter #(.width(3), .max('h7)) counter_7 (
    .load(in_7), .Q({q9, q8, q7}), .carry(out_48), .clk(and_3_out));  // open: D, count, clr
  not not_7 (not_7_out, and_4_out);
  J_K_Flip_Flop j_k_ff_8 (.J(1'b1), .clk(q2), .K(1'b1), .Q(j_k_ff_8_q), .Qn(j_k_ff_8_qn));  // open: preset, en, reset
  not not_8 (not_8_out, q2);
  T_Flip_Flop t_ff_4 (.clk(in_out), .T(1'b1), .Q(q1_2), .Qn(u1_2));  // open: preset, reset, en
  T_Flip_Flop t_ff_5 (.clk(clock_3_out), .T(and_6_out), .Q(q3_4), .Qn(u3_4));  // open: preset, reset, en
  S_R_Flip_Flop s_r_ff_1 (
    .S(and_4_out), .clk(clock_5_out), .R(not_7_out), .Q(s_r_ff_1_q));  // open: Qn, preset, reset, en
  J_K_Flip_Flop j_k_ff_9 (
    .J(j_k_ff_8_q), .clk(not_8_out), .K(j_k_ff_8_qn), .Q(q3), .Qn(u3));  // open: preset, en, reset
  T_Flip_Flop t_ff_6 (.clk(q1_2), .T(1'b1), .Q(q2_2), .Qn(u2_2));  // open: preset, reset, en
  Clock clock_9 (.out(clock_9_out));
  ROM #(.dataWidth(7)) rom_1 (.addr(counter_6_q), .data(rom_1_data));  // open: sel
  T_Flip_Flop t_ff_7 (.clk(clock_9_out), .T(clock_9_out), .Q(t_ff_7_q));  // open: Qn, preset, reset, en
  TTY tty_1 (.data(rom_1_data), .clk(clock_8_out), .clr(in_4));  // open: we
  T_Flip_Flop t_ff_8 (.clk(q2_2), .T(1'b1), .Q(q3_2), .Qn(u3_2));  // open: preset, reset, en
  T_Flip_Flop t_ff_9 (.clk(clock_9_out), .T(t_ff_7_q), .Q(q1_5), .Qn(u1_5));  // open: preset, reset, en
  and and_7 (and_7_out, in_8, q4_2);
  and and_8 (and_8_out, q1_5, t_ff_7_q);
  or or_1 (or_1_out, q1_7, and_7_out);
  or or_2 (or_2_out, q2_8, and_7_out);
  J_K_Flip_Flop j_k_ff_10 (
    .J(1'b1), .clk(in_1), .K(1'b1), .Q(j_k_ff_10_q), .Qn(j_k_ff_10_qn));  // open: preset, en, reset
  not not_9 (not_9_out, in_1);
  J_K_Flip_Flop j_k_ff_11 (
    .J(1'b1), .clk(in_1), .K(1'b1), .Q(j_k_ff_11_q), .Qn(j_k_ff_11_qn));  // open: preset, en, reset
  T_Flip_Flop t_ff_10 (.clk(clock_9_out), .T(and_8_out), .Q(q2_5), .Qn(u2_5));  // open: preset, reset, en
  J_K_Flip_Flop j_k_ff_12 (
    .J(j_k_ff_10_q), .clk(not_9_out), .K(j_k_ff_10_qn), .Q(out_9));  // open: Qn, preset, en, reset
  J_K_Flip_Flop j_k_ff_13 (.J(j_k_ff_11_q), .clk(in_1), .K(j_k_ff_11_qn), .Q(out_13));  // open: Qn, preset, en, reset
  and and_9 (and_9_out, q2_5, and_8_out, t_ff_7_q);
  J_K_Flip_Flop j_k_ff_14 (
    .J(1'b1), .clk(in_8), .K(1'b1), .Q(j_k_ff_14_q), .Qn(j_k_ff_14_qn));  // open: preset, en, reset
  not not_10 (not_10_out, in_8);
  J_K_Flip_Flop j_k_ff_15 (
    .J(1'b1), .clk(or_1_out), .K(1'b1), .Q(j_k_ff_15_q), .Qn(j_k_ff_15_qn));  // open: preset, en, reset
  not not_11 (not_11_out, or_1_out);
  J_K_Flip_Flop j_k_ff_16 (
    .J(1'b1), .clk(or_2_out), .K(1'b1), .Q(j_k_ff_16_q), .Qn(j_k_ff_16_qn));  // open: preset, en, reset
  not not_12 (not_12_out, or_2_out);
  J_K_Flip_Flop j_k_ff_17 (
    .J(1'b1), .clk(q3_8), .K(1'b1), .Q(j_k_ff_17_q), .Qn(j_k_ff_17_qn));  // open: preset, en, reset
  not not_13 (not_13_out, q3_8);
  T_Flip_Flop t_ff_11 (.clk(clock_9_out), .T(and_9_out), .Q(q3_5), .Qn(u3_5));  // open: preset, reset, en
  J_K_Flip_Flop j_k_ff_18 (
    .J(j_k_ff_14_q), .clk(not_10_out), .K(j_k_ff_14_qn), .Q(q1_7));  // open: Qn, preset, en, reset
  J_K_Flip_Flop j_k_ff_19 (
    .J(j_k_ff_15_q), .clk(not_11_out), .K(j_k_ff_15_qn), .Q(q2_8));  // open: Qn, preset, en, reset
  J_K_Flip_Flop j_k_ff_20 (
    .J(j_k_ff_16_q), .clk(not_12_out), .K(j_k_ff_16_qn), .Q(q3_8));  // open: Qn, preset, en, reset
  J_K_Flip_Flop j_k_ff_21 (
    .J(j_k_ff_17_q), .clk(not_13_out), .K(j_k_ff_17_qn), .Q(q4_2));  // open: Qn, preset, en, reset

  // Notes on the sheet:
  //   Обратный счёт
  //   Прямой счёт
  //   Прямой счёт
  //   Обратный счёт
  //   Счётчик с цепью группового переноса
  //   Тут что-то не так
  //   Прямой счёт
  //   Обратный счёт
  //   Счётчик с модулем 10
  //   Разрядов 4
  //   Обратный счёт
  //   Код гашения: 10 = 1010
  //   Прямой счёт
  //   contents of rom_1 (hex, n*v repeats v):
  //   48 65 6c 6c 6f 2c 20 77 6f 72 6c 64 21
  //   Счётчик с коэффициентом переноса 10
  //   Считает 0-8 плюс переполнение
  //   Прямой счёт
  //   Обратный счёт
endmodule
