// Logisim project D.circ as structural Verilog: 1 circuit, main circuit main
module main (
  input  D,
  input  C,
  input  D_2,
  input  C_2,
  input  C_3,
  input  C_4,
  input  D_3,
  input  D_4,
  input  in_9,
  input  D_5,
  input  Csyn,
  input  C_5,
  input  in_13,
  output Q1,
  output Q2,
  output Q1_2,
  output Q2_2,
  output Q1_3,
  output Q1_4,
  output Q2_3,
  output Q2_4,
  output Q1_5,
  output Q2_5
);

  wire nand_1_out, nand_2_out, nand_3_out, nand_4_out, nand_7_out, nand_8_out, nand_9_out, nand_10_out,
       nand_11_out, not_1_out;

  nand nand_1 (nand_1_out, D, C);
  nand nand_2 (nand_2_out, nand_1_out, C);
  nand nand_3 (nand_3_out, D_2, C_2);
  nand nand_4 (nand_4_out, nand_3_out, C_2);
  not not_1 (not_1_out, D_5);
  nand nand_5 (Q1, nand_1_out, Q2);
  nand nand_6 (Q2, Q1, nand_2_out);
  nand nand_7 (nand_7_out, nand_3_out, nand_8_out);
  nand nand_8 (nand_8_out, nand_7_out, nand_4_out);
  D_Flip_Flop d_ff_1 (.clk(C_3), .D(D_3), .Q(Q1_3), .Qn(Q2_3));  // open: preset, en, reset
  S_R_Flip_Flop s_r_ff_1 (.S(D_5), .clk(C_5), .R(not_1_out), .Q(Q1_5), .Qn(Q2_5));  // open: preset, reset, en
  not nand_9 (nand_9_out, C_2);  // NAND_Gate
  nand nand_10 (nand_10_out, nand_7_out, nand_9_out);
  nand nand_11 (nand_11_out, nand_10_out, nand_9_out);
  D_Flip_Flop T (.clk(C_4), .D(D_4), .Q(Q1_4), .Qn(Q2_4), .preset(in_9), .en(Csyn), .reset(in_13));
  nand nand_12 (Q1_2, nand_10_out, Q2_2);
  nand nand_13 (Q2_2, Q1_2, nand_11_out);
endmodule
