// Logisim project DigAut.circ as structural Verilog: 1 circuit, main circuit main
module main (
  input  z1,
  input  z2,
  input  C,
  output Y1,
  output Y2,
  output Q1,
  output Q2
);

  wire and_1_out, and_2_out, and_3_out, and_4_out, and_5_out, and_6_out, and_7_out, and_8_out, and_9_out,
       and_10_out, and_11_out, and_12_out, and_13_out, not_1_out, not_2_out, or_1_out, or_2_out, or_3_out,
       Q1_qn, Q2_qn;

  not not_1 (not_1_out, z1);
  not not_2 (not_2_out, z2);
  and and_1 (and_1_out, Q1_qn, not_1_out, Q2);
  and and_2 (and_2_out, z1, not_2_out, Q2_qn);
  and and_3 (and_3_out, not_1_out, Q1_qn);
  and and_4 (and_4_out, not_2_out, Q2_qn);
  and and_5 (and_5_out, Q1, not_2_out);
  and and_6 (and_6_out, z1, Q1_qn, Q2);
  or or_1 (or_1_out, and_1_out, and_2_out);
  or or_2 (or_2_out, and_3_out, and_4_out);
  or or_3 (or_3_out, and_5_out, and_6_out);
  S_R_Flip_Flop u_Q1 (.S(or_1_out), .clk(C), .R(Q1), .Q(Q1), .Qn(Q1_qn));  // open: preset, reset, en
  S_R_Flip_Flop u_Q2 (.S(or_2_out), .clk(C), .R(or_3_out), .Q(Q2), .Qn(Q2_qn));  // open: preset, reset, en
  and and_7 (and_7_out, z2, Q1);
  and and_8 (and_8_out, z1, z2, Q2_qn);
  and and_9 (and_9_out, z1, not_2_out, Q1_qn, Q2);
  and and_10 (and_10_out, not_1_out, Q1_qn, Q2);
  and and_11 (and_11_out, not_1_out, z2, Q2);
  and and_12 (and_12_out, z1, z2, Q2_qn);
  and and_13 (and_13_out, z1, not_2_out, Q1);
  or or_4 (Y1, and_7_out, and_8_out, and_9_out);
  or or_5 (Y2, and_10_out, and_11_out, and_12_out, and_13_out);
endmodule
