// Logisim project DigAutWithoutY.circ as structural Verilog: 1 circuit, main circuit main
module main (
  input  z1,
  input  z2,
  input  C,
  output q1,
  output q2
);

  wire and_1_out, and_2_out, and_3_out, and_4_out, and_5_out, and_6_out, not_1_out, not_2_out, or_1_out,
       or_2_out, or_3_out, Q1_qn, Q2_qn;

  not not_1 (not_1_out, z1);
  not not_2 (not_2_out, z2);
  and and_1 (and_1_out, Q1_qn, not_1_out, q2);
  and and_2 (and_2_out, z1, not_2_out, Q2_qn);
  and and_3 (and_3_out, not_1_out, Q1_qn);
  and and_4 (and_4_out, not_2_out, Q2_qn);
  and and_5 (and_5_out, q1, not_2_out);
  and and_6 (and_6_out, z1, Q1_qn, q2);
  or or_1 (or_1_out, and_1_out, and_2_out);
  or or_2 (or_2_out, and_3_out, and_4_out);
  or or_3 (or_3_out, and_5_out, and_6_out);
  S_R_Flip_Flop u_Q1 (.S(or_1_out), .clk(C), .R(q1), .Q(q1), .Qn(Q1_qn));  // open: preset, reset, en
  S_R_Flip_Flop u_Q2 (.S(or_2_out), .clk(C), .R(or_3_out), .Q(q2), .Qn(Q2_qn));  // open: preset, reset, en
endmodule
