// Logisim project DigAutY2.circ as structural Verilog: 1 circuit, main circuit main
module main (
  input  z1,
  input  z2,
  input  Q1,
  input  Q2,
  output y2
);

  wire and_1_out, and_2_out, and_3_out, and_4_out, not_1_out, not_2_out, not_3_out, not_4_out;

  not not_1 (not_1_out, z1);
  not not_2 (not_2_out, Q1);
  not not_3 (not_3_out, Q2);
  not not_4 (not_4_out, z2);
  and and_1 (and_1_out, not_1_out, not_2_out, Q2);
  and and_2 (and_2_out, not_1_out, z2, Q2);
  and and_3 (and_3_out, z1, z2, not_3_out);
  and and_4 (and_4_out, z1, not_4_out, Q1);
  or or_1 (y2, and_1_out, and_2_out, and_3_out, and_4_out);
endmodule
