// Logisim project JK.circ as structural Verilog: 1 circuit, main circuit main
module main (
  input  S,
  input  C,
  input  R,
  input  J,
  input  C_2,
  input  K,
  output out_7,
  output out_8,
  output Q1,
  output Q2
);

  wire and_1_out, and_2_out, not_1_out, s_r_ff_1_q, s_r_ff_1_qn;

  and and_1 (and_1_out, out_8, S);
  and and_2 (and_2_out, R, out_7);
  J_K_Flip_Flop j_k_ff_1 (.J(J), .clk(C_2), .K(K), .Q(Q1), .Qn(Q2));  // open: preset, en, reset
  S_R_Flip_Flop s_r_ff_1 (
    .S(and_1_out), .clk(C), .R(and_2_out), .Q(s_r_ff_1_q), .Qn(s_r_ff_1_qn));  // open: preset, reset, en
  not not_1 (not_1_out, C);
  S_R_Flip_Flop s_r_ff_2 (
    .S(s_r_ff_1_q), .clk(not_1_out), .R(s_r_ff_1_qn), .Q(out_7), .Qn(out_8));  // open: preset, reset, en
endmodule
