// Logisim project RG.circ as structural Verilog: 1 circuit, main circuit main
module main (
  input  C,
  input  C_2,
  input  C_3,
  input  D0,
  input  D0_2,
  input  D1,
  input  DSR,
  input  D2,
  input  C_4,
  input  D3,
  input  DSR_2,
  input  in_12,
  input  \Влево ,
  input  DSR_3,
  input  \Вправо ,
  input  \Сдвиг ,
  input  DI,
  input  D0_3,
  input  D1_2,
  input  D2_2,
  input  D3_2,
  input  V,
  input  C_5,
  output Q0,
  output Q0_2,
  output Q,
  output Q1,
  output Q1_2,
  output Q2,
  output Q2_2,
  output Q3,
  output Q3_2,
  output Q_2,
  output \К_другим_устройствам ,
  output \К_другим_устройствам_2 ,
  output Q0_3,
  output Q1_3,
  output Q2_3,
  output Q3_3
);

  wire and_1_out, and_2_out, and_3_out, and_4_out, and_5_out, and_6_out, and_7_out, and_8_out, and_9_out,
       and_10_out, and_11_out, and_12_out, d_ff_9_q, d_ff_14_q, d_ff_16_q, d_ff_17_q, d_ff_18_q, d_ff_19_q,
       d_ff_20_q, d_ff_22_q, not_1_out, not_2_out, or_1_out, or_2_out, or_3_out, or_4_out, or_5_out, or_6_out;

  D_Flip_Flop d_ff_1 (.clk(C), .D(D0), .Q(Q0));  // open: Qn, preset, en, reset
  D_Flip_Flop d_ff_2 (.clk(C), .D(D1), .Q(Q1));  // open: Qn, preset, en, reset
  D_Flip_Flop d_ff_3 (.clk(C), .D(D2), .Q(Q2));  // open: Qn, preset, en, reset
  D_Flip_Flop d_ff_4 (.clk(C), .D(D3), .Q(Q3));  // open: Qn, preset, en, reset
  not not_1 (not_1_out, V);
  and and_1 (and_1_out, d_ff_18_q, \Влево );
  and and_2 (and_2_out, DSR_3, \Вправо );
  not not_2 (not_2_out, not_1_out);
  or or_1 (or_1_out, and_1_out, and_2_out);
  and and_3 (and_3_out, DI, not_1_out);
  and and_4 (and_4_out, not_2_out, D0_3);
  and and_5 (and_5_out, Q0_3, not_1_out);
  and and_6 (and_6_out, not_2_out, D1_2);
  and and_7 (and_7_out, Q1_3, not_1_out);
  and and_8 (and_8_out, not_2_out, D2_2);
  and and_9 (and_9_out, Q2_3, not_1_out);
  and and_10 (and_10_out, not_2_out, D3_2);
  D_Flip_Flop d_ff_5 (.clk(C_2), .D(D0_2), .Q(Q0_2));  // open: Qn, preset, en, reset
  D_Flip_Flop d_ff_6 (.clk(C_2), .D(Q0_2), .Q(Q1_2));  // open: Qn, preset, en, reset
  D_Flip_Flop d_ff_7 (.clk(C_2), .D(Q1_2), .Q(Q2_2));  // open: Qn, preset, en, reset
  D_Flip_Flop d_ff_8 (.clk(C_2), .D(Q2_2), .Q(Q3_2));  // open: Qn, preset, en, reset
  D_Flip_Flop d_ff_9 (.clk(\Сдвиг ), .D(or_1_out), .Q(d_ff_9_q));  // open: Qn, preset, en, reset
  D_Flip_Flop d_ff_10 (.clk(C_5), .D(or_2_out), .Q(Q0_3));  // open: Qn, preset, en, reset
  or or_2 (or_2_out, and_3_out, and_4_out);
  D_Flip_Flop d_ff_11 (.clk(C_5), .D(or_3_out), .Q(Q1_3));  // open: Qn, preset, en, reset
  or or_3 (or_3_out, and_5_out, and_6_out);
  D_Flip_Flop d_ff_12 (.clk(C_5), .D(or_4_out), .Q(Q2_3));  // open: Qn, preset, en, reset
  or or_4 (or_4_out, and_7_out, and_8_out);
  D_Flip_Flop d_ff_13 (.clk(C_5), .D(or_5_out), .Q(Q3_3));  // open: Qn, preset, en, reset
  or or_5 (or_5_out, and_9_out, and_10_out);
  and and_11 (and_11_out, in_12, \Влево );
  and and_12 (and_12_out, d_ff_9_q, \Вправо );
  D_Flip_Flop d_ff_14 (.clk(C_3), .D(DSR), .Q(d_ff_14_q));  // open: Qn, preset, en, reset
  D_Flip_Flop d_ff_15 (.clk(C_4), .D(d_ff_17_q), .Q(Q_2));  // open: Qn, preset, en, reset
  or or_6 (or_6_out, and_11_out, and_12_out);
  D_Flip_Flop d_ff_16 (.clk(C_3), .D(d_ff_14_q), .Q(d_ff_16_q));  // open: Qn, preset, en, reset
  D_Flip_Flop d_ff_17 (.clk(C_4), .D(d_ff_20_q), .Q(d_ff_17_q));  // open: Qn, preset, en, reset
  D_Flip_Flop d_ff_18 (.clk(\Сдвиг ), .D(or_6_out), .Q(d_ff_18_q));  // open: Qn, preset, en, reset
  D_Flip_Flop d_ff_19 (.clk(C_3), .D(d_ff_16_q), .Q(d_ff_19_q));  // open: Qn, preset, en, reset
  D_Flip_Flop d_ff_20 (.clk(C_4), .D(d_ff_22_q), .Q(d_ff_20_q));  // open: Qn, preset, en, reset
  D_Flip_Flop d_ff_21 (.clk(C_3), .D(d_ff_19_q), .Q(Q));  // open: Qn, preset, en, reset
  D_Flip_Flop d_ff_22 (.clk(C_4), .D(DSR_2), .Q(d_ff_22_q));  // open: Qn, preset, en, reset

  assign \К_другим_устройствам  = \Влево ;
  assign \К_другим_устройствам_2  = \Вправо ;

  // Notes on the sheet:
  //   От других устройств
endmodule
