// Logisim project RSc.circ as structural Verilog: 1 circuit, main circuit main
module main (
  input  S,
  input  R,
  input  S_2,
  input  C,
  input  R_2,
  input  S0,
  input  S_3,
  input  C_2,
  input  R_3,
  input  R0,
  output Q1,
  output Q2,
  output Q1_2,
  output Q2_2,
  output Q1_3,
  output Q2_3
);

  wire nand_1_out, nand_2_out, nand_5_out, nand_6_out, nand_7_out, nand_8_out, nand_9_out, nand_10_out;

  not nand_1 (nand_1_out, S);  // NAND_Gate
  not nand_2 (nand_2_out, R);  // NAND_Gate
  nand nand_3 (Q1, nand_1_out, Q2);
  nand nand_4 (Q2, Q1, nand_2_out);
  nand nand_5 (nand_5_out, S_2, C);
  nand nand_6 (nand_6_out, C, R_2);
  not nand_7 (nand_7_out, S0);  // NAND_Gate
  nand nand_8 (nand_8_out, S_3, C_2);
  nand nand_9 (nand_9_out, C_2, R_3);
  not nand_10 (nand_10_out, R0);  // NAND_Gate
  nand nand_11 (Q1_2, nand_5_out, Q2_2);
  nand nand_12 (Q2_2, Q1_2, nand_6_out);
  nand nand_13 (Q1_3, nand_7_out, nand_8_out, Q2_3);
  nand nand_14 (Q2_3, Q1_3, nand_9_out, nand_10_out);
endmodule
