// Logisim project RScSet2t.circ as structural Verilog: 1 circuit, main circuit main
module main (
  input  S,
  input  C,
  input  R,
  input  S0,
  input  S_2,
  input  C_2,
  input  R_2,
  input  R0,
  input  S_3,
  input  C_3,
  input  R_3,
  output Q1,
  output Q2,
  output Q1_2,
  output Q2_2,
  output Q1_3,
  output out_17
);

  wire and_1_out, and_2_out, and_3_out, and_4_out, nand_1_out, nand_2_out, nand_3_out, nand_4_out,
       nand_5_out, nand_6_out, nand_7_out, nand_8_out, nor_1_out, nor_2_out, not_1_out, not_2_out, not_3_out,
       s_r_ff_1_q, s_r_ff_1_qn;

  and and_1 (and_1_out, S, C);
  and and_2 (and_2_out, C, R);
  not nand_1 (nand_1_out, S0);  // NAND_Gate
  nand nand_2 (nand_2_out, S_2, C_2);
  nand nand_3 (nand_3_out, C_2, R_2);
  not nand_4 (nand_4_out, R0);  // NAND_Gate
  S_R_Flip_Flop s_r_ff_1 (.S(S_3), .clk(C_3), .R(R_3), .Q(s_r_ff_1_q), .Qn(s_r_ff_1_qn));  // open: preset, reset, en
  not not_1 (not_1_out, C_3);
  nor nor_1 (nor_1_out, and_1_out, nor_2_out);
  nor nor_2 (nor_2_out, nor_1_out, and_2_out);
  not not_2 (not_2_out, C);
  nand nand_5 (nand_5_out, nand_1_out, nand_2_out, nand_6_out);
  nand nand_6 (nand_6_out, nand_5_out, nand_3_out, nand_4_out);
  not not_3 (not_3_out, C_2);
  S_R_Flip_Flop s_r_ff_2 (
    .S(s_r_ff_1_q), .clk(not_1_out), .R(s_r_ff_1_qn), .Q(Q1_3), .Qn(out_17));  // open: preset, reset, en
  and and_3 (and_3_out, nor_1_out, not_2_out);
  and and_4 (and_4_out, not_2_out, nor_2_out);
  nand nand_7 (nand_7_out, nand_5_out, not_3_out);
  nand nand_8 (nand_8_out, not_3_out, nand_6_out);
  nor nor_3 (Q1, and_3_out, Q2);
  nor nor_4 (Q2, Q1, and_4_out);
  nand nand_9 (Q1_2, nand_1_out, nand_7_out, Q2_2);
  nand nand_10 (Q2_2, Q1_2, nand_8_out, nand_4_out);
endmodule
