// Logisim project RScSetInp.circ as structural Verilog: 1 circuit, main circuit main
module main (
  input  S,
  input  C,
  input  R,
  input  S0,
  input  Csyn,
  input  R0,
  output Q1,
  output Q2
);

  S_R_Flip_Flop T (.S(S), .clk(C), .R(R), .Q(Q1), .Qn(Q2), .preset(S0), .reset(R0), .en(Csyn));
endmodule
