// Logisim project RScSetInpScheme.circ as structural Verilog: 1 circuit, main circuit main
module main (
  input  S0,
  input  R,
  input  C,
  input  S,
  input  R0,
  output Q1,
  output Q2
);

  wire and_1_out, and_2_out;

  and and_1 (and_1_out, R, C);
  and and_2 (and_2_out, C, S);
  nor nor_1 (Q1, S0, and_1_out, Q2);
  nor nor_2 (Q2, Q1, and_2_out, R0);
endmodule
