// Logisim project test.circ as structural Verilog: 1 circuit, main circuit main
module main (
  input  x1,
  input  x2,
  input  x3,
  output out_4
);

  wire nand_1_out, nand_2_out, nand_3_out, nand_4_out, not_1_out, not_2_out, not_3_out;

  not not_1 (not_1_out, x1);
  not not_2 (not_2_out, x2);
  not not_3 (not_3_out, x3);
  nand nand_1 (nand_1_out, not_1_out, not_2_out, x3);
  nand nand_2 (nand_2_out, not_1_out, x2, x3);
  nand nand_3 (nand_3_out, x1, not_2_out, x3);
  nand nand_4 (nand_4_out, x1, x2, not_3_out);
  nand nand_5 (out_4, nand_1_out, nand_2_out, nand_3_out, nand_4_out);
endmodule
