// Logisim project test3.circ as structural Verilog: 1 circuit, main circuit main
module main (
  input  z1,
  input  z2,
  input  C,
  output q1,
  output q2,
  output y1,
  output y2
);

  wire and_1_out, and_2_out, and_3_out, and_4_out, and_5_out, and_6_out, and_7_out, and_8_out, and_9_out,
       and_10_out, and_11_out, and_12_out, and_13_out, not_1_out, not_2_out, or_1_out, or_2_out, s_r_ff_1_qn,
       s_r_ff_2_qn;

  not not_1 (not_1_out, z1);
  not not_2 (not_2_out, z2);
  and and_1 (and_1_out, q1, not_2_out, not_1_out);
  and and_2 (and_2_out, not_1_out, z2, s_r_ff_1_qn);
  and and_3 (and_3_out, s_r_ff_1_qn, not_2_out, z1);
  and and_4 (and_4_out, not_1_out, not_2_out, q2, s_r_ff_2_qn);
  and and_5 (and_5_out, not_1_out, s_r_ff_1_qn);
  and and_6 (and_6_out, z1, z2);
  or or_1 (or_1_out, and_6_out, and_7_out);
  and and_7 (and_7_out, not_2_out, not_1_out, q2);
  or or_2 (or_2_out, and_2_out, and_3_out, and_4_out);
  S_R_Flip_Flop s_r_ff_1 (.S(and_5_out), .clk(C), .R(or_1_out), .Q(q2), .Qn(s_r_ff_1_qn));  // open: preset, reset, en
  S_R_Flip_Flop s_r_ff_2 (.S(or_2_out), .clk(C), .R(and_1_out), .Q(q1), .Qn(s_r_ff_2_qn));  // open: preset, reset, en
  and and_8 (and_8_out, not_1_out, not_2_out);
  and and_9 (and_9_out, z1, q1);
  and and_10 (and_10_out, z1, not_2_out);
  or or_3 (y1, and_8_out, and_9_out, and_10_out);
  and and_11 (and_11_out, s_r_ff_2_qn, s_r_ff_1_qn);
  and and_12 (and_12_out, not_1_out, z2, s_r_ff_2_qn);
  and and_13 (and_13_out, z1, not_2_out, q1);
  or or_4 (y2, and_11_out, and_12_out, and_13_out);
endmodule
