// Logisim project tmp1.circ as structural Verilog: 1 circuit, main circuit main
module main (
  input  B,
  input  in_2,
  output w1,
  output w2
);

  wire A1_q, A1_qn, A2_q, A2_qn, and_1_out, and_2_out, and_3_out, and_4_out, and_5_out, and_6_out, and_7_out,
       and_8_out, not_1_out, or_1_out;

  not not_1 (not_1_out, B);
  and and_1 (and_1_out, A2_qn, A1_qn, not_1_out);
  and and_2 (and_2_out, A2_qn, B, A1_q);
  or or_1 (or_1_out, and_1_out, and_2_out);
  and and_3 (and_3_out, B, A1_q, A2_qn);
  and and_4 (and_4_out, A1_qn, A2_q, B);
  S_R_Flip_Flop A1 (.clk(in_2), .R(and_3_out), .Q(A1_q), .Qn(A1_qn));  // open: S, preset, reset, en
  S_R_Flip_Flop A2 (.S(or_1_out), .clk(in_2), .R(and_4_out), .Q(A2_q), .Qn(A2_qn));  // open: preset, reset, en
  and and_5 (and_5_out, B, A1_qn, A2_qn);
  or or_2 (w1, and_5_out, and_6_out);
  and and_6 (and_6_out, B, A1_qn, A2_q);
  and and_7 (and_7_out, A1_qn, A2_q);
  or or_3 (w2, and_7_out, and_8_out);
  and and_8 (and_8_out, A1_q, A2_qn, B);
endmodule
