// Logisim project ИБазис1.circ as structural Verilog: 1 circuit, main circuit main
module main (
  input  x1,
  input  x2,
  input  x3,
  output p
);

  wire nor_1_out, nor_2_out, nor_3_out, not_1_out;

  not not_1 (not_1_out, x3);
  nor nor_1 (nor_1_out, x1, x2);
  nor nor_2 (nor_2_out, x1, not_1_out);
  nor nor_3 (nor_3_out, nor_1_out, nor_2_out);
  not not_2 (p, nor_3_out);
endmodule
