// Logisim project Основные функции.circ as structural Verilog: 1 circuit, main circuit main
module main (
  input  x,
  input  x1,
  input  x2,
  input  x1_2,
  input  x2_2,
  input  x1_3,
  input  x2_3,
  input  x1_4,
  input  x2_4,
  output p,
  output p_2,
  output p_3,
  output p_4,
  output p_5
);

  not not_1 (p, x);
  and and_1 (p_2, x1, x2);
  or or_1 (p_3, x1_2, x2_2);
  nand nand_1 (p_4, x1_3, x2_3);
  nor nor_1 (p_5, x1_4, x2_4);
endmodule
