// Logisim project Сумматор.circ as structural Verilog: 1 circuit, main circuit main
module main (
  input  P_minus,
  input  A,
  input  B,
  input  A_2,
  input  C,
  input  in_6,
  input  C_2,
  input  A_3,
  input  in_9,
  input  B_2,
  input  D,
  input  B_3,
  input  in_13,
  input  A_4,
  input  B_4,
  input  P_minus_2,
  input  \Cвх ,
  input  A0,
  input  B0,
  input  A1,
  input  B1,
  input  A2,
  input  B2,
  input  \Cвх_2 ,
  input  A0_2,
  input  B0_2,
  input  A1_2,
  input  B1_2,
  input  A2_2,
  input  B2_2,
  input  A3,
  input  B3,
  input  \Cвх_3 ,
  input  A0_3,
  input  B0_3,
  input  A1_3,
  input  B1_3,
  input  A2_3,
  input  B2_3,
  input  \Cвх_4 ,
  input  A0_4,
  input  B0_4,
  input  A1_4,
  input  B1_4,
  input  A2_4,
  input  B2_4,
  input  A3_2,
  input  B3_2,
  output S0,
  output P0,
  output S,
  output S1,
  output P,
  output P1,
  output S_2,
  output P_plus,
  output S0_2,
  output S1_2,
  output S2,
  output S3,
  output S0_3,
  output S1_3,
  output S2_2,
  output S3_2
);

  wire adder_3_cout, adder_3_out, and_1_out, and_2_out, and_4_out, and_5_out, and_6_out, and_7_out,
       and_8_out, and_9_out, and_10_out, d_ff_1_q, nand_1_out, nand_2_out, nand_3_out, nand_4_out,
       nand_5_out, nand_6_out, nand_7_out, nand_8_out, nand_9_out, nand_10_out, nand_11_out, nand_12_out,
       nand_13_out, nand_14_out, nand_15_out, nand_16_out, nand_17_out, nand_18_out, nand_19_out,
       nand_20_out, nand_21_out, nand_22_out, nand_23_out, nand_24_out, nand_25_out, nand_26_out,
       nand_27_out, nand_28_out, nand_29_out, nand_30_out, nand_31_out, nand_32_out, nand_33_out,
       nand_34_out, nand_35_out, nand_36_out, not_1_out, not_2_out, not_3_out, not_4_out, not_5_out,
       not_6_out, not_7_out, not_8_out, not_9_out, not_10_out, not_11_out, not_12_out, not_13_out,
       not_14_out, not_15_out, not_16_out, not_17_out, shift_register_1_out, shift_register_2_out;

  not not_1 (not_1_out, A);
  not not_2 (not_2_out, B);
  not not_3 (not_3_out, P_minus_2);
  not not_4 (not_4_out, B_4);
  not not_5 (not_5_out, A_4);
  and and_1 (and_1_out, not_1_out, B);
  and and_2 (and_2_out, A, not_2_out);
  and and_3 (P, B, A);
  or or_1 (S, and_1_out, and_2_out);
  and and_4 (and_4_out, not_5_out, not_4_out, P_minus_2);
  and and_5 (and_5_out, not_5_out, B_4, not_3_out);
  and and_6 (and_6_out, A_4, not_4_out, not_3_out);
  and and_7 (and_7_out, A_4, B_4, P_minus_2);
  and and_8 (and_8_out, A_4, B_4);
  and and_9 (and_9_out, A_4, P_minus_2);
  and and_10 (and_10_out, B_4, P_minus_2);
  or or_2 (S_2, and_4_out, and_5_out, and_6_out, and_7_out);
  or or_3 (P_plus, and_8_out, and_9_out, and_10_out);
  Adder #(.width(1)) adder_1 (.a(A_3), .b(B_3), .out(S0), .cin(P_minus), .cout(P0));
  Adder #(.width(1)) adder_2 (.a(C_2), .b(D), .out(S1), .cin(P0), .cout(P1));
  Shift_Register #(.length(3)) shift_register_1 (
    .in(A_2), .clk(C), .out(shift_register_1_out), .clr(in_6));  // open: shift, load, d0, q0, d1, q1, d2, q2
  Shift_Register #(.length(3)) shift_register_2 (
    .in(B_2), .clk(C), .out(shift_register_2_out), .clr(in_13));  // open: shift, load, d0, q0, d1, q1, d2, q2
  not not_6 (not_6_out, A0);
  not not_7 (not_7_out, B0);
  not not_8 (not_8_out, A1);
  not not_9 (not_9_out, B1);
  not not_10 (not_10_out, A2);
  not not_11 (not_11_out, B2);
  not not_12 (not_12_out, A0_3);
  not not_13 (not_13_out, B0_3);
  not not_14 (not_14_out, A1_3);
  not not_15 (not_15_out, B1_3);
  not not_16 (not_16_out, A2_3);
  not not_17 (not_17_out, B2_3);
  Adder #(.width(1)) adder_3 (
    .a(shift_register_1_out), .b(shift_register_2_out), .out(adder_3_out), .cin(d_ff_1_q), .cout(adder_3_cout));
  D_Flip_Flop d_ff_1 (.clk(C), .D(adder_3_cout), .Q(d_ff_1_q));  // open: Qn, preset, en, reset
  Shift_Register #(.length(3)) shift_register_3 (
    .in(adder_3_out), .clk(C), .clr(in_9));  // open: shift, out, load, d0, q0, d1, q1, d2, q2
  nand nand_1 (nand_1_out, not_6_out, B0);
  nand nand_2 (nand_2_out, A0, not_7_out);
  nand nand_3 (nand_3_out, not_8_out, B1);
  nand nand_4 (nand_4_out, A1, not_9_out);
  nand nand_5 (nand_5_out, not_10_out, B2);
  nand nand_6 (nand_6_out, A2, not_11_out);
  nand nand_7 (nand_7_out, A0, B0);
  nand nand_8 (nand_8_out, nand_28_out, \Cвх );
  nand nand_9 (nand_9_out, A1, B1);
  nand nand_10 (nand_10_out, nand_29_out, A0, B0);
  nand nand_11 (nand_11_out, nand_29_out, nand_28_out, \Cвх );
  nand nand_12 (nand_12_out, A2, B2);
  nand nand_13 (nand_13_out, nand_30_out, B1, A1);
  nand nand_14 (nand_14_out, nand_30_out, nand_29_out, A0, B0, A1);
  nand nand_15 (nand_15_out, nand_30_out, nand_29_out, nand_28_out, \Cвх );
  nand nand_16 (nand_16_out, not_12_out, not_13_out);
  nand nand_17 (nand_17_out, not_14_out, not_15_out);
  nand nand_18 (nand_18_out, not_16_out, not_17_out);
  nand nand_19 (nand_19_out, A0_3, B0_3);
  nand nand_20 (nand_20_out, nand_16_out, \Cвх_3 );
  nand nand_21 (nand_21_out, A1_3, B1_3);
  nand nand_22 (nand_22_out, nand_17_out, A0_3, B0_3);
  nand nand_23 (nand_23_out, nand_17_out, nand_16_out, \Cвх_3 );
  nand nand_24 (nand_24_out, A2_3, B2_3);
  nand nand_25 (nand_25_out, nand_18_out, B1_3, A1_3);
  nand nand_26 (nand_26_out, nand_18_out, nand_17_out, A0_3, B0_3);
  nand nand_27 (nand_27_out, nand_18_out, nand_17_out, nand_16_out, \Cвх_3 );
  nand nand_28 (nand_28_out, nand_1_out, nand_2_out);
  nand nand_29 (nand_29_out, nand_3_out, nand_4_out);
  nand nand_30 (nand_30_out, nand_5_out, nand_6_out);
  nand nand_31 (nand_31_out, nand_7_out, nand_8_out);
  nand nand_32 (nand_32_out, nand_9_out, nand_10_out, nand_11_out);
  nand nand_33 (nand_33_out, nand_12_out, nand_13_out, nand_14_out, nand_15_out);
  nand nand_34 (nand_34_out, nand_19_out, nand_20_out);
  nand nand_35 (nand_35_out, nand_21_out, nand_22_out, nand_23_out);
  nand nand_36 (nand_36_out, nand_24_out, nand_25_out, nand_26_out, nand_27_out);
  Adder #(.width(1)) adder_4 (.a(A0_4), .b(B0_4), .out(S0_3), .cin(\Cвх_4 ));  // open: cout
  Adder #(.width(1)) adder_5 (.a(A1_4), .b(B1_4), .out(S1_3), .cin(nand_34_out));  // open: cout
  Adder #(.width(1)) adder_6 (.a(A2_4), .b(B2_4), .out(S2_2), .cin(nand_35_out));  // open: cout
  Adder #(.width(1)) adder_7 (.a(A3_2), .b(B3_2), .out(S3_2), .cin(nand_36_out));  // open: cout
  Adder #(.width(1)) adder_8 (.a(A0_2), .b(B0_2), .out(S0_2), .cin(\Cвх_2 ));  // open: cout
  Adder #(.width(1)) adder_9 (.a(A1_2), .b(B1_2), .out(S1_2), .cin(nand_31_out));  // open: cout
  Adder #(.width(1)) adder_10 (.a(A2_2), .b(B2_2), .out(S2), .cin(nand_32_out));  // open: cout
  Adder #(.width(1)) adder_11 (.a(A3), .b(B3), .out(S3), .cin(nand_33_out));  // open: cout

  // Notes on the sheet:
  //   h0
  //   h1
  //   h2
  //   h0
  //   h1
  //   h2
  //   C0
  //   C1
  //   C0
  //   C1
  //   C2
  //   C2
endmodule
