// Logisim project Шифраторы.circ as structural Verilog: 1 circuit, main circuit main
module main (
  input  x1,
  input  x2,
  input  x3,
  input  x4,
  input  x5,
  input  x6,
  input  x7,
  output y4,
  output y4_2,
  output y4_3
);

  wire and_1_out, and_2_out, and_3_out, and_4_out, and_5_out, and_6_out, and_7_out, and_8_out, and_9_out,
       and_10_out, and_11_out, and_12_out, not_1_out, not_2_out, not_3_out, not_4_out, not_5_out, not_6_out,
       not_7_out;

  not not_1 (not_1_out, x1);
  not not_2 (not_2_out, x2);
  not not_3 (not_3_out, x3);
  not not_4 (not_4_out, x4);
  not not_5 (not_5_out, x5);
  not not_6 (not_6_out, x6);
  not not_7 (not_7_out, x7);
  and and_1 (and_1_out, not_1_out, not_2_out, not_3_out, x4, not_5_out, not_6_out, not_7_out);
  and and_2 (and_2_out, not_1_out, not_2_out, not_3_out, not_4_out, x5, not_6_out, not_7_out);
  and and_3 (and_3_out, not_1_out, not_2_out, not_3_out, not_4_out, not_5_out, x6, not_7_out);
  and and_4 (and_4_out, not_1_out, not_2_out, not_3_out, not_4_out, not_5_out, not_6_out, x7);
  and and_5 (and_5_out, not_1_out, x2, not_3_out, not_4_out, not_5_out, not_6_out, not_7_out);
  and and_6 (and_6_out, not_1_out, not_2_out, x3, not_4_out, not_5_out, not_6_out, not_7_out);
  and and_7 (and_7_out, not_1_out, not_2_out, not_3_out, not_4_out, not_5_out, x6, not_7_out);
  and and_8 (and_8_out, not_1_out, not_2_out, not_3_out, not_4_out, not_5_out, not_6_out, x7);
  and and_9 (and_9_out, x1, not_2_out, not_3_out, not_4_out, not_5_out, not_6_out, not_7_out);
  and and_10 (and_10_out, not_1_out, not_2_out, x3, not_4_out, not_5_out, not_6_out, not_7_out);
  and and_11 (and_11_out, not_1_out, not_2_out, not_3_out, not_4_out, x5, not_6_out, not_7_out);
  and and_12 (and_12_out, not_1_out, not_2_out, not_3_out, not_4_out, not_5_out, not_6_out, x7);
  or or_1 (y4, and_1_out, and_2_out, and_3_out, and_4_out);
  or or_2 (y4_2, and_5_out, and_6_out, and_7_out, and_8_out);
  or or_3 (y4_3, and_9_out, and_10_out, and_11_out, and_12_out);
endmodule
