// Logisim project оснБазис1.circ as structural Verilog: 1 circuit, main circuit main
module main (
  input  x1,
  input  x2,
  input  x3,
  output p
);

  wire and_1_out, not_1_out, not_2_out, or_1_out;

  or or_1 (or_1_out, x1, x2);
  not not_1 (not_1_out, x1);
  not not_2 (not_2_out, or_1_out);
  and and_1 (and_1_out, not_1_out, x3);
  or or_2 (p, not_2_out, and_1_out);
endmodule
